# Fritzing sketch conexiones_sin_booster (saved by Fritzing 0.9.3b)
breadboards: 1

parts:
  J1 = Basic Servo
  J2 = Basic Servo
  M2 = DC Motor
  VCC1 = Battery  # not connected
  V1 = DC Power [voltage=5]  # not connected
  Pololu_A1 = Pololu A4988 [package=SO16]
  M1 = DC Motor
  U1 = SWITCH_SPDT [package=kps-1290]
  J3 = Basic Servo
  U2 = TRANSCHIPTC5747 [package=camera_sfv24r-2st_2]
  MCU1 = Raspberry Pi Zero
  Componente3 = USB LiPoly Charger  # not connected

nets:
  GND: J1.gnd, J2.gnd, Pololu_A1.MS3, J3.gnd, MCU1.pin_5
  VCC: J1.vcc, J2.vcc, Pololu_A1.RESET, U1.P, J3.vcc, MCU1.pin_2, MCU1.pin_4
  N1: J1.pulse, MCU1.pin_23
  N2: J2.pulse, MCU1.pin_21
  N3: M2.pin_1, Pololu_A1.1A
  N4: M2.pin_2, Pololu_A1.1B
  N5: Pololu_A1.MS1, MCU1.pin_11
  N6: Pololu_A1.MS2, MCU1.pin_12
  N7: Pololu_A1.SLEEP, MCU1.pin_16
  N8: Pololu_A1.STEP, MCU1.pin_15
  N9: Pololu_A1.2A, M1.pin_2
  N10: Pololu_A1.2B, M1.pin_1
  N11: J3.pulse, MCU1.pin_19
  N12: U2.SCLK, U2.AGND, U2.AVDD28, U2.RESET_N
  N13: U2.DOUT_0, U2.DOUT_1, U2.DOUT_2, U2.DOUT_3, U2.DOUT_4
  N14: U2.DOUT_7, U2.DOUT_8, U2.VCLK_OUT, U2.VALIDH, U2.VALIDV
  N15: U2.PS1, U2.PS2, U2.SHIELD, U2.LED_CTRL
  N16: MCU1.pin_1, MCU1.pin_17
  N17: MCU1.pin_9, MCU1.pin_25, MCU1.pin_39

notes:
  2x18650 en Paralelo
  TP4056 Cargador
  DRV8833
  Motor 1: GPIO 17 y 18
  Motor 2: GPIO 22 y 23
  Servos dirección y pasajeros
  PiCamera
  100uF
